# Fritzing sketch dual_lights (saved by Fritzing 0.9.3b)
breadboards: 1

parts:
  Part1 = FTDI Basic Programmer
  C1 = Electrolytic Capacitor [capacitance=1µF package="100 mil [THT, electrolytic]"]
  R1 = Resistor [tolerance=±5% resistance=10k package=THT]
  R2 = Resistor [tolerance=±5% resistance=10k package=THT]
  S1 = Pushbutton [package="[THT]"]
  S2 = Pushbutton [package="[THT]"]
  C2 = Capacitor [package=cap-pth-small2]
  R3 = Resistor [tolerance=±5% resistance=10k package=THT]
  U2 = ESP8266 WiFi Module [part_number=ESP8266]
  U3 = ESP8266 WiFi Module [part_number=ESP8266]  # not connected
  KY-1 = Keyes Relay [package=THT]
  KY-2 = Keyes Relay [package=THT]
  S3 = Pushbutton [package="[THT]"]
  C3 = Capacitor [package=cap-pth-small2]

nets:
  N1: Part1.RXI, U2.TXD
  N2: Part1.TXO, U2.RXD
  N3: Part1.POWER, C1.+, R1.Pin_1, R2.Pin_1, C2.2, R3.Pin_0, U2.VCC, KY-1.power, KY-2.power
  GND: Part1.GND, C1.-, S1.Pin_3, S1.Pin_4, S2.Pin_3, S2.Pin_4, C2.1, U2.GND, U2.GPIO_15, KY-1.ground, KY-2.ground, S3.Pin_3, S3.Pin_4, C3.2
  N4: R1.Pin_0, S1.Pin_1, S1.Pin_2, U2.GPIO_0
  N5: R2.Pin_0, S2.Pin_1, S2.Pin_2, U2.REST
  N6: R3.Pin_1, U2.CH_PD
  N7: U2.GPIO_4, S3.Pin_1, S3.Pin_2, C3.1
  N8: U2.GPIO_5, KY-1.signal
  N9: U2.GPIO_12, KY-2.signal

notes:
  PROGRAM
  RESET
  https://www.studiopieters.nl
  RST
  ADC
  CH_PD
  GPIO16
  GPIO14
  GPIO12
  GPIO13
  VCC
  TXD
  GPIO4
  GPIO0
  GPIO5
  GPIO15
  GPIO2
  GND
  CS0
  MOSI
  GPIO10
  GPIO9
  SCLK
  MISO
  BUTTON
  RELAY 0 / LAMP1
  RELAY 1 / LAMP2

custom parts:
  FTDI Basic Programmer: Description: This is the newest revision of our FTDI Basic. We now use a SMD 6-pin header on the bottom, which makes it smaller and more compact. Functionality has remained the same. This is a basic breakout board for the FTDI FT232RL USB to serial IC. The pinout of this board matches the FTDI cable to work with official Arduino and cloned 3.3V Arduino boards. It can also be used for general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
  ESP8266 WiFi Module: Generic WiFi Module based on the ESP8266 with onboard PCB antenna and UART communications
  Keyes Relay: The Keyes 5V relay module is suitable for SCM development, home appliance control. It uses a 5V~12V TIL control signal which can control DC / AC signal.
